# Fritzing sketch BBB_BMP180 (saved by Fritzing 0.9.3b)
breadboards: 1

parts:
  BeagleBone1 = BeagleBone Black
  Part1 = Adafruit BMP180
  R1 = Resistor [tolerance=±5% resistance=220 package="2512 [SMD]"]
  R2 = Resistor [tolerance=±5% resistance=220 package="2512 [SMD]"]

nets:
  N1: BeagleBone1.no_name_yet#1, Part1.GND
  N2: BeagleBone1.no_name_yet#3, Part1.+5V, R1.Pin_1, R2.Pin_1
  N3: BeagleBone1.no_name_yet#19, Part1.SCL, R2.Pin_0
  N4: BeagleBone1.no_name_yet#20, Part1.SDA, R1.Pin_0

custom parts:
  BeagleBone Black: BeagleBone Black rev. A5B
  Adafruit BMP180: This precision sensor from Bosch is the best low-cost sensing solution for measuring barometric pressure and temperature. Because pressure changes with altitude you can also use it as an altimeter! The sensor is soldered onto a PCB with a 3.3V regulator, I2C level shifter and pull-up resistors on the I2C pins. The BMP180 is the next-generation of sensors from Bosch, and replaces the BMP085.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
